# Fritzing sketch arduino_sound (saved by Fritzing 0.9.3b)

parts:
  Arduino_Uno_R3 = Arduino Uno (Rev3)
  Toggle_Switch = Toggle Switch [package=THT]
  Potentiometer = Rotary Potentiometer (Small) [maximum_resistance=100kΩ package=THT]
  Piezoelectric_Buzzer = Piezo Speaker

nets:
  N1: Arduino_Uno_R3.D5_PWM, Toggle_Switch.L1
  N2: Arduino_Uno_R3.GND, Piezoelectric_Buzzer.pin2
  N3: Toggle_Switch.COM, Toggle_Switch.L2, Potentiometer.wiper
  N4: Potentiometer.leg2, Piezoelectric_Buzzer.pin1
